# Fritzing sketch bugbot (saved by Fritzing 0.9.9b)
breadboards: 1

parts:
  PWM1 = PCA9685 16x12-bit PWM Breakout
  Part1 = Arduino Nano (Rev3.0)
  U1 = LIPO-2000mAh [package=lipo-2000]
  J1 = Basic Servo

nets:
  N1: PWM1.no_name_yet#0, J1.pulse
  N2: PWM1.no_name_yet#100, PWM1.no_name_yet#505, PWM1.no_name_yet#706, Part1.VIN, U1.+
  N3: PWM1.no_name_yet#501, PWM1.no_name_yet#701, PWM1.no_name_yet#1000, Part1.GND, U1.-
  N4: PWM1.no_name_yet#503, Part1.A5
  N5: PWM1.no_name_yet#504, Part1.A4
